# Fritzing sketch button-and-led (saved by Fritzing 0.8.3b)
breadboards: 1

parts:
  Raspberry_Pi_rev1 = Raspberry Pi rev2
  LED1 = smd LED [color="Red (633nm)" package="0805 [SMD]"]
  R1 = Resistor [tolerance=±5% resistance=220 package=THT]
  S1 = Pushbutton [package="[THT]"]

nets:
  N1: Raspberry_Pi_rev1.3V3, S1.Pin_3, S1.Pin_4
  N2: Raspberry_Pi_rev1.GND, R1.Pin_1
  N3: Raspberry_Pi_rev1.GPIO_17, S1.Pin_1, S1.Pin_2
  N4: Raspberry_Pi_rev1.GPIO_18, LED1.cathode
  N5: LED1.anode, R1.Pin_0

notes:
  Controlling LED using Button in Raspberry Pi
  https://github.com/sudar/raspberry-pi-sketches
  http://hardwarefun.com
