# Fritzing sketch button-input (saved by Fritzing 0.8.3b)
breadboards: 1

parts:
  Raspberry_Pi_rev1 = Raspberry Pi rev2
  S1 = Pushbutton [package="[THT]"]

nets:
  N1: Raspberry_Pi_rev1.3V3, S1.Pin_2
  N2: Raspberry_Pi_rev1.GPIO_17, S1.Pin_4

notes:
  Reading button status from Raspberry Pi
  https://github.com/sudar/raspberry-pi-sketches
  http://hardwarefun.com
